// Logisim project relogio.circ as structural Verilog
// 0a9
module contar0a9 (
  input  CLK,
  input  Reset,
  output [3:0] \Saída ,
  output CLK_seguinte
);

  wire or_1_out;
  wire [3:0] adder_1_out;

  Register #(.width(4)) register_1 (.D(adder_1_out), .Q(\Saída ), .clk(CLK), .clr(or_1_out));  // open: en
  or or_1 (or_1_out, CLK_seguinte, Reset);
  Hex_Digit_Display hex_digit_display_1 (.value(\Saída ));  // open: dp
  Adder #(.width(4)) adder_1 (.a(\Saída ), .b(4'b0001), .out(adder_1_out));  // open: cin, cout
  nor NOR (CLK_seguinte, \Saída [0], ~\Saída [1], \Saída [2], ~\Saída [3]);  // NOR_Gate

  // Notes on the sheet:
  //   CLK: pull=up
endmodule

module contador0a59 (
  input  CLK,
  input  Reset,
  output [3:0] unidade,
  output [3:0] Dezena,
  output CLK_seguinte
);

  wire contar0a9_2_clk_seguinte, OR_out;

  Hex_Digit_Display hex_digit_display_1 (.value(Dezena));  // open: dp
  contar0a9 contar0a9_1 (.CLK(contar0a9_2_clk_seguinte), .Reset(OR_out), .\Saída (Dezena));  // open: CLK_seguinte
  nor NOR (CLK_seguinte, Dezena[3], ~Dezena[2], ~Dezena[1], Dezena[0], unidade[3], unidade[2], unidade[1], unidade[0]);  // NOR_Gate
  Hex_Digit_Display hex_digit_display_2 (.value(unidade));  // open: dp
  contar0a9 contar0a9_2 (.CLK(CLK), .Reset(OR_out), .\Saída (unidade), .CLK_seguinte(contar0a9_2_clk_seguinte));
  or OR (OR_out, CLK_seguinte, Reset);
endmodule

module cantador0a23 (
  input  CLK,
  input  Reset,
  output [3:0] unidade,
  output [3:0] Dezena,
  output CLK_seguinte
);

  wire contar0a9_2_clk_seguinte, OR_out;

  Hex_Digit_Display hex_digit_display_1 (.value(Dezena));  // open: dp
  contar0a9 contar0a9_1 (.CLK(contar0a9_2_clk_seguinte), .Reset(OR_out), .\Saída (Dezena));  // open: CLK_seguinte
  nor NOR (CLK_seguinte, Dezena[3], Dezena[2], ~Dezena[1], Dezena[0], unidade[3], ~unidade[2], unidade[1], unidade[0]);  // NOR_Gate
  Hex_Digit_Display hex_digit_display_2 (.value(unidade));  // open: dp
  contar0a9 contar0a9_2 (.CLK(CLK), .Reset(OR_out), .\Saída (unidade), .CLK_seguinte(contar0a9_2_clk_seguinte));
  or OR (OR_out, CLK_seguinte, Reset);
endmodule

module _12a12 (
  input  CLK,
  input  Reset,
  output [3:0] uni,
  output [3:0] dez
);

  wire contar0a9_2_clk_seguinte, NOR_2_out, NOR_out, OR_out;
  wire [3:0] \contar0a9_1_saída , \contar0a9_2_saída ;

  Hex_Digit_Display hex_digit_display_1 (.value(dez));  // open: dp
  Multiplexer #(.width(4), .enable("false")) multiplexer_1 (
    .in0(\contar0a9_1_saída ), .in1(4'b0001), .out(dez), .sel(NOR_2_out));
  contar0a9 contar0a9_1 (
    .CLK(contar0a9_2_clk_seguinte), .Reset(OR_out), .\Saída (\contar0a9_1_saída ));  // open: CLK_seguinte
  nor NOR (NOR_out, \contar0a9_1_saída [3], \contar0a9_1_saída [2], \contar0a9_1_saída [1], ~\contar0a9_1_saída [0], \contar0a9_2_saída [3], \contar0a9_2_saída [2], ~\contar0a9_2_saída [1], \contar0a9_2_saída [0]);  // NOR_Gate
  Hex_Digit_Display hex_digit_display_2 (.value(uni));  // open: dp
  Multiplexer #(.width(4), .enable("false")) multiplexer_2 (
    .in0(\contar0a9_2_saída ), .in1(4'b0010), .out(uni), .sel(NOR_2_out));
  contar0a9 contar0a9_2 (
    .CLK(CLK), .Reset(OR_out), .\Saída (\contar0a9_2_saída ), .CLK_seguinte(contar0a9_2_clk_seguinte));
  or OR (OR_out, NOR_out, Reset);
  nor NOR_2 (NOR_2_out, \contar0a9_2_saída [0], \contar0a9_2_saída [1], \contar0a9_2_saída [2], \contar0a9_2_saída [3], \contar0a9_1_saída [0], \contar0a9_1_saída [1], \contar0a9_1_saída [2], \contar0a9_1_saída [3]);
endmodule

module ctk_am_pm_24h (
  input  AM_PM_e_24H,
  input  CLK,
  output [3:0] un,
  output [3:0] Dez
);

  wire d_ff_1_q, subtractor_1_out, undriven;
  wire [3:0] _0a23_dezena, _0a23_unidade, _12a12_p1, _12a12_p2;

  D_Flip_Flop d_ff_1 (.clk(AM_PM_e_24H), .D(subtractor_1_out), .Q(d_ff_1_q));  // open: Qn, preset, en, reset
  Subtractor #(.width(1)) subtractor_1 (.a(d_ff_1_q), .b(1'b1), .out(subtractor_1_out));  // open: bin, bout
  Hex_Digit_Display hex_digit_display_1 (.value(Dez));  // open: dp
  Multiplexer #(.width(4), .enable("false")) multiplexer_1 (
    .in0(_12a12_p1), .in1(_0a23_dezena), .out(Dez), .sel(undriven));
  // _12a12 _12a12: pin names not known; wires that end beside it: _12a12_p1, _12a12_p2, CLK
  Hex_Digit_Display hex_digit_display_2 (.value(un));  // open: dp
  Multiplexer #(.width(4), .enable("false")) multiplexer_2 (
    .in0(_12a12_p2), .in1(_0a23_unidade), .out(un), .sel(d_ff_1_q));
  cantador0a23 _0a23 (.Dezena(_0a23_dezena), .unidade(_0a23_unidade), .CLK(CLK));  // open: CLK_seguinte, Reset

  // Notes on the sheet:
  //   un: pull=down
  //   CLK: pull=up
  //   Dez: pull=down
endmodule

module principal (
);

  wire _0a59_2_clk_seguinte, _0a59_clk_seguinte, clock_1_out;
  wire [3:0] _0a23_dezena, _0a23_unidade, _0a59_2_dezena, _0a59_2_unidade, _0a59_dezena, _0a59_unidade;

  Hex_Digit_Display hex_digit_display_1 (.value(_0a23_dezena));  // open: dp
  Hex_Digit_Display hex_digit_display_2 (.value(_0a23_unidade));  // open: dp
  cantador0a23 _0a23 (
    .Dezena(_0a23_dezena), .unidade(_0a23_unidade), .CLK(_0a59_clk_seguinte));  // open: CLK_seguinte, Reset
  Hex_Digit_Display hex_digit_display_3 (.value(_0a59_dezena));  // open: dp
  Hex_Digit_Display hex_digit_display_4 (.value(_0a59_unidade));  // open: dp
  contador0a59 _0a59 (
    .CLK_seguinte(_0a59_clk_seguinte), .Dezena(_0a59_dezena), .unidade(_0a59_unidade),
    .CLK(_0a59_2_clk_seguinte));  // open: Reset
  Hex_Digit_Display hex_digit_display_5 (.value(_0a59_2_dezena));  // open: dp
  Hex_Digit_Display hex_digit_display_6 (.value(_0a59_2_unidade));  // open: dp
  contador0a59 _0a59_2 (
    .CLK_seguinte(_0a59_2_clk_seguinte), .Dezena(_0a59_2_dezena), .unidade(_0a59_2_unidade), .CLK(clock_1_out));  // open: Reset
  Clock clock_1 (.out(clock_1_out));
endmodule
